// Logisim project jjz4_hw4.circ as structural Verilog: 12 circuits, main circuit main
module main (
  input  in_1
);

  wire alu_1__0, alu_1__0_2, ALUSrc, and_1_out, and_2_out, blt, bne, Clk, jal, jr, Jump, keyboard, MemRead,
       MemtoReg, MemWrite, not_1_out, not_2_out, not_3_out, or_1_out, or_2_out, or_3_out, RegDest, RegWrite,
       TTY;
  wire [2:0] multiplexer_3_out, multiplexer_6_out, RD, RS, RT, Shamt;
  wire [3:0] OpCode, signextender_1_output;
  wire [5:0] Immediate;
  wire [6:0] keyboard_1_data;
  wire [11:0] Address, pc_1_output;
  wire [15:0] adder_1_output, adder_2_output, alu_1_out_8, multiplexer_1_out, multiplexer_2_out,
       multiplexer_4_out, multiplexer_5_out, multiplexer_7_out, multiplexer_8_out, multiplexer_9_out, out,
       pc_1_output_2, ram_1_data, registerfile_1_p8, rom_1_data;

  Clock clock_1 (.out(Clk));
  Multiplexer #(.width(16)) multiplexer_1 (
    .in0(multiplexer_7_out), .in1(pc_1_output_2), .out(multiplexer_1_out), .sel(or_1_out));  // open: en
  or or_1 (or_1_out, jal, Jump);
  Keyboard keyboard_1 (.clk(Clk), .re(keyboard), .data(keyboard_1_data));  // open: clr, avail
  PC pc_1 (.in_1(multiplexer_1_out), .in_3(in_1), .Output({pc_1_output_2[15:12], pc_1_output}), .in_2(Clk));
  adder adder_1 (
    .in_1(16'h1), .in_2({pc_1_output_2[15:12], pc_1_output}), .in_3(1'b0), .Output(adder_1_output));  // open: C_out
  ROM #(.addrWidth(16), .dataWidth(16)) rom_1 (
    .addr({pc_1_output_2[15:12], pc_1_output}), .data(rom_1_data));  // open: sel
  adder adder_2 (
    .in_1(adder_1_output), .in_2({signextender_1_output, pc_1_output_2[11:0]}), .in_3(1'b0),
    .Output(adder_2_output));  // open: C_out
  Multiplexer #(.width(16)) multiplexer_2 (
    .in0(multiplexer_9_out), .in1(adder_1_output), .out(multiplexer_2_out), .sel(jal));  // open: en
  Multiplexer #(.width(3)) multiplexer_3 (.in0(RT), .in1(RD), .out(multiplexer_3_out), .sel(RegDest));  // open: en
  Multiplexer #(.width(16)) multiplexer_4 (
    .in0(adder_1_output), .in1(adder_2_output), .out(multiplexer_4_out), .sel(or_2_out));  // open: en
  Multiplexer #(.width(16)) multiplexer_5 (
    .in0(multiplexer_2_out), .in1({{9{1'b0}}, keyboard_1_data}), .out(multiplexer_5_out), .sel(keyboard));  // open: en
  not not_1 (not_1_out, Clk);
  Multiplexer #(.width(3)) multiplexer_6 (
    .in0(multiplexer_3_out), .in1(3'b111), .out(multiplexer_6_out), .sel(jal));  // open: en
  Multiplexer #(.width(16)) multiplexer_7 (
    .in0(multiplexer_4_out), .in1(out), .out(multiplexer_7_out), .sel(jr));  // open: en
  not not_2 (not_2_out, Clk);
  TTY tty_1 (.data(out[6:0]), .clk(not_2_out), .we(TTY));  // open: clr
  Decoder Decoder (
    .in_1(rom_1_data), .OpCode(OpCode), .RS(RS), .RT(RT), .RD(RD), .Shamt(Shamt), .Immediate(Immediate),
    .Address(Address));
  // RegisterFile registerfile_1: pin names not known; wires that end beside it: multiplexer_5_out, not_1_out, RegWrite, multiplexer_6_out, RS, RT, out, registerfile_1_p8
  SignExtender signextender_1 (.Input(Immediate), .Output({signextender_1_output, pc_1_output_2[11:0]}));
  Multiplexer #(.width(16)) multiplexer_8 (
    .in0(registerfile_1_p8), .in1({signextender_1_output, pc_1_output_2[11:0]}), .out(multiplexer_8_out),
    .sel(ALUSrc));  // open: en
  or or_2 (or_2_out, or_3_out, jal);
  Control Control (
    .OpCode(OpCode), .RegDst(RegDest), .ALUSrc(ALUSrc), .MemToReg(MemtoReg), .RegWrite(RegWrite),
    .MemRead(MemRead), .MemWrite(MemWrite), .bne(bne), .Jump(Jump), .jr(jr), .jal(jal), .keyboard(keyboard),
    .TTY(TTY), .blt(blt));
  ALU alu_1 (
    .in_1(out), .in_2(OpCode[2:0]), .in_3(multiplexer_8_out), .in_4(Shamt), .out_8(alu_1_out_8),
    ._0(alu_1__0), ._0_2(alu_1__0_2));  // open: Overflow
  or or_3 (or_3_out, and_1_out, and_2_out);
  not not_3 (not_3_out, Clk);
  and and_1 (and_1_out, alu_1__0_2, bne);
  and and_2 (and_2_out, blt, alu_1__0);
  RAM #(.addrWidth(16), .dataWidth(16), .bus("separate")) ram_1 (
    .addr(alu_1_out_8), .din(registerfile_1_p8), .data(ram_1_data), .str(MemWrite), .clk(not_3_out),
    .clr(in_1));  // open: sel, ld
  Multiplexer #(.width(16)) multiplexer_9 (
    .in0(alu_1_out_8), .in1(ram_1_data), .out(multiplexer_9_out), .sel(MemtoReg));  // open: en

  // Other names for the same wires on the sheet: Reset = in_1

  // Notes on the sheet:
  //   1. Set clock high
  //   2. Hit reset bit twice
  //   3. Set clock low.
  //   4. Execute program.
  //   How to execute a program on this processor:
  //   contents of rom_1 (hex, n*v repeats v):
  //   1241 9281 16c2 1243 a444 1904 91ff 1fc1 91ff 1b45 91ff 1fc1 91ff
endmodule

module adder (
  input  [15:0] in_1,
  input  [15:0] in_2,
  input  in_3,
  output [15:0] Output,
  output C_out
);

  wire n4_bit_adder_1_c_out, n4_bit_adder_2_c_out, n4_bit_adder_3_c_out;

  _4_bit_adder u_4_bit_adder_1 (
    .Input_A(in_1[3:0]), .Input_B(in_2[3:0]), .Carry(in_3), .C_out(n4_bit_adder_1_c_out), .Output(Output[3:0]));
  _4_bit_adder u_4_bit_adder_2 (
    .Input_A(in_1[7:4]), .Input_B(in_2[7:4]), .Carry(n4_bit_adder_1_c_out), .C_out(n4_bit_adder_2_c_out),
    .Output(Output[7:4]));
  _4_bit_adder u_4_bit_adder_3 (
    .Input_A(in_1[11:8]), .Input_B(in_2[11:8]), .Carry(n4_bit_adder_2_c_out), .C_out(n4_bit_adder_3_c_out),
    .Output(Output[11:8]));
  _4_bit_adder u_4_bit_adder_4 (
    .Input_A(in_1[15:12]), .Input_B(in_2[15:12]), .Carry(n4_bit_adder_3_c_out), .C_out(C_out),
    .Output(Output[15:12]));

  // Other names for the same wires on the sheet: Initial_Carry = in_3; Input_A[15:0] = in_1; Input_B[15:0] = in_2
endmodule

module ALU (
  input  [15:0] in_1,
  input  [2:0] in_2,
  input  [15:0] in_3,
  input  [2:0] in_4,
  output _0,
  output _0_2,
  output Overflow,
  output [15:0] out_8
);

  wire and_1_out, undriven;
  wire [14:0] adder_2_output;
  wire [15:0] adder_output, not_1_out, not_2_out, Shift_Left_out_3, Shift_Right_out_3, xor_1_out;

  assign not_1_out = ~in_3;  // NOT_Gate not_1, 16 bits wide
  adder adder (.in_1(in_1), .in_2(in_3), .in_3(1'b0), .Output(adder_output));  // open: C_out
  adder adder_2 (.in_1(in_1), .in_2(not_1_out), .in_3(1'b1), .C_out(Overflow), .Output({_0, adder_2_output}));
  assign not_2_out = ~in_1;  // NOT_Gate not_2, 16 bits wide
  assign xor_1_out = in_1 ^ in_3;  // XOR_Gate xor_1, 16 bits wide
  SLL Shift_Left (.in_1(in_1), .in_2(in_4), .out_3(Shift_Left_out_3));
  SRL Shift_Right (.in_1(in_1), .in_2(in_4), .out_3(Shift_Right_out_3));
  Multiplexer #(.select(3), .width(16)) multiplexer_1 (
    .in0(adder_output), .in1(adder_output), .in2({_0, adder_2_output}), .in3(not_2_out), .in4(xor_1_out),
    .in5(Shift_Left_out_3), .in6(Shift_Right_out_3), .out(out_8), .sel(in_2), .en(undriven));  // open: in7
  and and_1 (and_1_out, ~adder_2_output[0], ~adder_2_output[1], ~adder_2_output[2], ~adder_2_output[3], ~adder_2_output[4], ~adder_2_output[5], ~adder_2_output[6], ~adder_2_output[7], ~adder_2_output[8], ~adder_2_output[9], ~adder_2_output[10], ~adder_2_output[11], ~adder_2_output[12], ~adder_2_output[13], ~adder_2_output[14], ~_0);  // AND_Gate
  not not_3 (_0_2, and_1_out);

  // Other names for the same wires on the sheet: ALU_Select[2:0] = in_2; Input_A[15:0] = in_1; Input_B[15:0] = in_3;
  //   Shift_Amount[2:0] = in_4
endmodule

module _1_bit_adder (
  input  A,
  input  B,
  input  Carry,
  output out_4,
  output C_out
);

  wire and_1_out, and_2_out, xor_1_out;

  xor xor_1 (xor_1_out, A, B);
  and and_1 (and_1_out, xor_1_out, Carry);
  and and_2 (and_2_out, A, B);
  xor xor_2 (out_4, xor_1_out, Carry);
  or or_1 (C_out, and_1_out, and_2_out);
endmodule

module SLL (
  input  [15:0] in_1,
  input  [2:0] in_2,
  output [15:0] out_3
);

  wire [15:2] _2nd_Shift;
  wire [15:4] multiplexer_2_out;
  wire [15:12] multiplexer_2_out_2;
  wire [15:14] multiplexer_1_out;

  Multiplexer #(.width(16)) multiplexer_1 (
    .in0(in_1), .in1({in_1[14:0], 1'b0}), .out({multiplexer_1_out, _2nd_Shift}), .sel(in_2[0]));  // open: en
  Multiplexer #(.width(16)) multiplexer_2 (
    .in0({multiplexer_1_out, _2nd_Shift}), .in1({_2nd_Shift, 2'b00}),
    .out({multiplexer_2_out_2, multiplexer_2_out}), .sel(in_2[1]));  // open: en
  Multiplexer #(.width(16)) multiplexer_3 (
    .in0({multiplexer_2_out_2, multiplexer_2_out}), .in1({multiplexer_2_out, 4'b0000}), .out(out_3),
    .sel(in_2[2]));  // open: en

  // Other names for the same wires on the sheet: _1st_Shift[15:1] = in_1[14:0]; Input[15:0] = in_1;
  //   Shift_Amt[2:0] = in_2
endmodule

module SRL (
  input  [15:0] in_1,
  input  [2:0] in_2,
  output [15:0] out_3
);

  wire [1:0] multiplexer_1_out;
  wire [13:0] multiplexer_1_out_2;
  wire [15:0] multiplexer_2_out;

  Multiplexer #(.width(16)) multiplexer_1 (
    .in0(in_1), .in1({1'b0, in_1[15:1]}), .out({multiplexer_1_out_2, multiplexer_1_out}), .sel(in_2[0]));  // open: en
  Multiplexer #(.width(16)) multiplexer_2 (
    .in0({multiplexer_1_out_2, multiplexer_1_out}), .in1({2'b00, multiplexer_1_out_2}),
    .out(multiplexer_2_out), .sel(in_2[1]));  // open: en
  Multiplexer #(.width(16)) multiplexer_3 (
    .in0(multiplexer_2_out), .in1({4'b0000, multiplexer_2_out[15:4]}), .out(out_3), .sel(in_2[2]));  // open: en

  // Other names for the same wires on the sheet: Input[15:0] = in_1; Shift_Amt[2:0] = in_2
endmodule

module _4_bit_register (
  input  [3:0] Input,
  input  Clock,
  input  Reset,
  output [3:0] Output
);

  D_Flip_Flop d_ff_1 (.clk(Clock), .D(Input[0]), .Q(Output[0]), .reset(Reset));  // open: Qn, preset, en
  D_Flip_Flop d_ff_2 (.clk(Clock), .D(Input[1]), .Q(Output[1]), .reset(Reset));  // open: Qn, preset, en
  D_Flip_Flop d_ff_3 (.clk(Clock), .D(Input[2]), .Q(Output[2]), .reset(Reset));  // open: Qn, preset, en
  D_Flip_Flop d_ff_4 (.clk(Clock), .D(Input[3]), .Q(Output[3]), .reset(Reset));  // open: Qn, preset, en
endmodule

module PC (
  input  [15:0] in_1,
  input  in_2,
  input  in_3,
  output [15:0] Output
);

  _4_bit_register u_4_bit_register_1 (.Input(in_1[3:0]), .Reset(in_3), .Output(Output[3:0]), .Clock(in_2));
  _4_bit_register u_4_bit_register_2 (.Input(in_1[7:4]), .Reset(in_3), .Output(Output[7:4]), .Clock(in_2));
  _4_bit_register u_4_bit_register_3 (.Input(in_1[11:8]), .Reset(in_3), .Output(Output[11:8]), .Clock(in_2));
  _4_bit_register u_4_bit_register_4 (.Input(in_1[15:12]), .Reset(in_3), .Output(Output[15:12]), .Clock(in_2));

  // Other names for the same wires on the sheet: Clock = in_2; Reset = in_3
endmodule

module Decoder (
  input  [15:0] in_1,
  output [3:0] OpCode,
  output [2:0] RS,
  output [2:0] RT,
  output [2:0] RD,
  output [2:0] Shamt,
  output [5:0] Immediate,
  output [11:0] Address
);


  assign Address = in_1[11:0];
  assign Immediate = in_1[5:0];
  assign OpCode = in_1[15:12];
  assign RD = in_1[5:3];
  assign RS = in_1[11:9];
  assign RT = in_1[8:6];
  assign Shamt = in_1[2:0];
endmodule

module _4_bit_adder (
  input  [3:0] Input_A,
  input  Carry,
  input  [3:0] Input_B,
  output [3:0] Output,
  output C_out
);

  wire n1_bit_adder_1_c_out, n1_bit_adder_2_c_out, n1_bit_adder_3_c_out;

  _1_bit_adder u_1_bit_adder_1 (
    .A(Input_A[0]), .B(Input_B[0]), .Carry(Carry), .out_4(Output[0]), .C_out(n1_bit_adder_1_c_out));
  _1_bit_adder u_1_bit_adder_2 (
    .A(Input_A[1]), .B(Input_B[1]), .Carry(n1_bit_adder_1_c_out), .out_4(Output[1]),
    .C_out(n1_bit_adder_2_c_out));
  _1_bit_adder u_1_bit_adder_3 (
    .A(Input_A[2]), .B(Input_B[2]), .Carry(n1_bit_adder_2_c_out), .out_4(Output[2]),
    .C_out(n1_bit_adder_3_c_out));
  _1_bit_adder u_1_bit_adder_4 (
    .A(Input_A[3]), .B(Input_B[3]), .Carry(n1_bit_adder_3_c_out), .out_4(Output[3]), .C_out(C_out));
endmodule

module Control (
  input  [3:0] OpCode,
  output RegDst,
  output ALUSrc,
  output MemToReg,
  output RegWrite,
  output MemRead,
  output MemWrite,
  output bne,
  output Jump,
  output jr,
  output jal,
  output keyboard,
  output TTY,
  output blt
);

  wire add_out, addi, \not , sll_out, srl_out, sub_out, xor_out;

  and add (add_out, ~OpCode[0], ~OpCode[1], ~OpCode[2], ~OpCode[3]);  // AND_Gate
  and sub (sub_out, ~OpCode[0], OpCode[1], ~OpCode[2], ~OpCode[3]);  // AND_Gate
  and \xor  (xor_out, ~OpCode[0], ~OpCode[1], OpCode[2], ~OpCode[3]);  // AND_Gate
  and sll (sll_out, OpCode[0], ~OpCode[1], OpCode[2], ~OpCode[3]);  // AND_Gate
  and srl (srl_out, ~OpCode[0], OpCode[1], OpCode[2], ~OpCode[3]);  // AND_Gate
  and lw (MemRead, OpCode[0], OpCode[1], OpCode[2], ~OpCode[3]);  // AND_Gate
  and sw (MemWrite, ~OpCode[0], ~OpCode[1], ~OpCode[2], OpCode[3]);  // AND_Gate
  and u_addi (addi, OpCode[0], ~OpCode[1], ~OpCode[2], ~OpCode[3]);  // AND_Gate
  and u_not (\not , OpCode[0], OpCode[1], ~OpCode[2], ~OpCode[3]);  // AND_Gate
  and u_bne (bne, OpCode[0], ~OpCode[1], ~OpCode[2], OpCode[3]);  // AND_Gate
  and u_blt (blt, ~OpCode[0], OpCode[1], ~OpCode[2], OpCode[3]);  // AND_Gate
  and j (Jump, OpCode[0], OpCode[1], ~OpCode[2], OpCode[3]);  // AND_Gate
  and u_jr (jr, ~OpCode[0], ~OpCode[1], OpCode[2], OpCode[3]);  // AND_Gate
  and u_jal (jal, OpCode[0], ~OpCode[1], OpCode[2], OpCode[3]);  // AND_Gate
  and u_keyboard (keyboard, ~OpCode[0], OpCode[1], OpCode[2], OpCode[3]);  // AND_Gate
  and u_TTY (TTY, OpCode[0], OpCode[1], OpCode[2], OpCode[3]);
  or or_1 (RegDst, add_out, sub_out, xor_out, sll_out, srl_out);
  or or_2 (ALUSrc, MemRead, addi, \not , MemWrite);
  or or_3 (RegWrite, RegDst, addi, \not , MemRead, keyboard, jal);

  assign MemToReg = MemRead;

  // Other names for the same wires on the sheet: j = Jump; lw = MemRead; R = RegDst; sw = MemWrite
endmodule

// Sign Extender
module SignExtender (
  input  [5:0] Input,
  output [15:0] Output
);


  assign Output = {{11{Input[5]}}, Input[4:0]};
endmodule
